# Fritzing sketch LED_Blink_RevisitedFritzing (saved by Fritzing 0.9.3b)

parts:
  LED1 = LEDs [package=led10mm]
  Part1 = Arduino Uno (Rev3)

nets:
  N1: LED1.C, Part1.GND
  N2: LED1.A, Part1.D6_PWM
